# Fritzing sketch Protoboard-bolus-estacion-base (saved by Fritzing 0.9.3b)
breadboards: 1

parts:
  U1 = atmega328 [package=dip]
  T1 = LM35 Temperature Sensor [package="TO92 [THT]"]
  S1 = PH meter [package=THT]
  VCC1 = 4 x AAA Battery Mount
  U2 = LM358 [package=dip08]
  R1 = Resistor [tolerance=±5% resistance=1k package="1206 [SMD]"]
  R2 = Resistor [tolerance=±5% resistance=3.9k package="1206 [SMD]"]
  R4 = Rotary Potentiometer (Small) [maximum_resistance=100kΩ package=THT]
  U3 = XBEE-1 [package=xbee-1]
  U4 = XBEE-1 [package=xbee-1]
  Mod2 = Raspberry Pi 4B

nets:
  N1: U1.D0_(RX), U3.DIN
  N2: U1.D1_(TX), U3.DOUT
  VCC: U1.VCC, U1.AVCC, U1.AREF, T1.+Vs, S1.pin2, VCC1.+, U3.VDD
  GND: U1.GND, T1.GND, S1.pin3, VCC1.-, R1.Pin_1, U3.GND
  N3: U1.A0, U2.G$1_OUT, R4.leg1, R4.wiper
  N4: U1.A1, S1.pin1
  N5: T1.Vout, U2.G$1_+IN
  N6: U2.G$1_-IN, R1.Pin_0, R2.Pin_0
  N7: R2.Pin_1, R4.leg2
  VDD: U4.VDD, Mod2.3V3
  N8: U4.DIN, Mod2.GPIO15
  GND_2: U4.GND, Mod2.GND
